# Fritzing sketch 06_lab4_main3_3_diagram (saved by Fritzing 0.9.3b)
breadboards: 1

parts:
  J1 = STM32 Nucleo boards
  R1 = Resistor [tolerance=±5% resistance=220 package=THT]
  R2 = Resistor [tolerance=±5% resistance=220 package=THT]
  R3 = Resistor [tolerance=±5% resistance=220 package=THT]
  R4 = Resistor [tolerance=±5% resistance=220 package="0402 [SMD]"]
  S1 = Pushbutton [package=THT]
  S2 = Pushbutton [package=THT]
  S3 = Pushbutton [package=THT]
  S4 = Pushbutton [package=THT]

nets:
  N1: J1.GND, S1.leg1, S2.leg1, S3.leg1, S4.leg1
  N2: J1.PB8, R3.Pin_0, S3.leg0
  N3: J1.PB9, R2.Pin_0, S2.leg0
  N4: J1.PB10, R1.Pin_0, S1.leg0
  N5: J1.PB7, R4.Pin_0, S4.leg0
  N6: R1.Pin_1, R2.Pin_1, R3.Pin_1, R4.Pin_1
